# Fritzing sketch lm35-nodemcu (saved by Fritzing 0.8.7b)
breadboards: 2

parts:
  U1 = NodeMCU V3.0
  T1 = LM35 Temperature Sensor [package="TO92 [THT]"]

nets:
  N1: U1.3V3, T1.+Vs
  N2: U1.GND#6, U1.GND#13, U1.GND#16, U1.GND#33, T1.GND
  N3: U1.A0, T1.Vout

custom parts:
  NodeMCU V3.0: ESP8266 based NodeMCU
